// Logisim project register.circ as structural Verilog: 1 circuit, main circuit main
module main (
  input  Reset,
  input  [15:0] in_2
);

  wire clock_1_out;

  Clock clock_1 (.out(clock_1_out));
  D_Flip_Flop d_ff_1 (.clk(clock_1_out), .D(in_2[0]), .reset(Reset));  // open: Q, Qn, preset, en
  D_Flip_Flop d_ff_2 (.clk(clock_1_out), .D(in_2[1]), .reset(Reset));  // open: Q, Qn, preset, en
  D_Flip_Flop d_ff_3 (.clk(clock_1_out), .D(in_2[2]), .reset(Reset));  // open: Q, Qn, preset, en
  D_Flip_Flop d_ff_4 (.clk(clock_1_out), .D(in_2[3]));  // open: Q, Qn, preset, en, reset
  D_Flip_Flop d_ff_5 (.clk(clock_1_out), .D(in_2[4]), .reset(Reset));  // open: Q, Qn, preset, en
  D_Flip_Flop d_ff_6 (.clk(clock_1_out), .D(in_2[5]), .reset(Reset));  // open: Q, Qn, preset, en
  D_Flip_Flop d_ff_7 (.clk(clock_1_out), .D(in_2[6]), .reset(Reset));  // open: Q, Qn, preset, en
  D_Flip_Flop d_ff_8 (.clk(clock_1_out), .D(in_2[7]));  // open: Q, Qn, preset, en, reset
  D_Flip_Flop d_ff_9 (.clk(clock_1_out), .D(in_2[8]), .reset(Reset));  // open: Q, Qn, preset, en
  D_Flip_Flop d_ff_10 (.clk(clock_1_out), .D(in_2[9]), .reset(Reset));  // open: Q, Qn, preset, en
  D_Flip_Flop d_ff_11 (.clk(clock_1_out), .D(in_2[10]), .reset(Reset));  // open: Q, Qn, preset, en
  D_Flip_Flop d_ff_12 (.clk(clock_1_out), .D(in_2[11]));  // open: Q, Qn, preset, en, reset
  D_Flip_Flop d_ff_13 (.clk(clock_1_out), .D(in_2[12]), .reset(Reset));  // open: Q, Qn, preset, en
  D_Flip_Flop d_ff_14 (.clk(clock_1_out), .D(in_2[13]), .reset(Reset));  // open: Q, Qn, preset, en
  D_Flip_Flop d_ff_15 (.clk(clock_1_out), .D(in_2[14]), .reset(Reset));  // open: Q, Qn, preset, en
  D_Flip_Flop d_ff_16 (.clk(clock_1_out), .D(in_2[15]));  // open: Q, Qn, preset, en, reset

  // Other names for the same wires on the sheet: _0 = in_2[0]; _1 = in_2[1]; _2 = in_2[2]; _3 = in_2[3]; _4 = in_2[4];
  //   _5 = in_2[5]; _6 = in_2[6]; _7 = in_2[7]; _8 = in_2[8]; _9 = in_2[9]; _10 = in_2[10]; _11 = in_2[11];
  //   _12 = in_2[12]; _13 = in_2[13]; _14 = in_2[14]; _15 = in_2[15]
endmodule
