// Logisim project question6.circ as structural Verilog: 1 circuit, main circuit main
module main (
  input  in1,
  input  in2
);

  wire and_1_out, D0_Q0_qn, D1_Q1_q, or_1_out;

  buf and_1 (and_1_out, or_1_out);  // AND_Gate
  or or_1 (or_1_out, D1_Q1_q, D0_Q0_qn);
  D_Flip_Flop D1_Q1 (.D(and_1_out), .Q(D1_Q1_q));  // open: clk, Qn, preset, en, reset
  D_Flip_Flop D0_Q0 (.Qn(D0_Q0_qn));  // open: clk, D, Q, preset, en, reset
endmodule
